# Fritzing sketch Schema_CMG001A (saved by Fritzing 0.8.3b)
breadboards: 1

parts:
  kEYPAD_MATRICIAL_1 = KEYPAD 4x3
  J1 = Piezo Speaker
  K1 = Relay [part_number=FRS1B-S package=THT]
  S1 = Toggle Switch [package=THT]
  TRS1 = Audio Jack (TRS) 3.5mm [package="4Ucon 08780 [THT]"]
  S2 = Round Pushbutton
  R4 = Resistor [tolerance=±5% resistance=10k package=THT]
  Arduino1 = Arduino
  R7 = Resistor [tolerance=±5% resistance=330 package=THT]
  R6 = Rotary Potentiometer (Small) [maximum_resistance=100kΩ]
  LCD1 = Adafruit Negative RGB 2x16 LCD
  R8 = Rotary Potentiometer (Small) [maximum_resistance=100kΩ]
  R9 = Rotary Potentiometer (Small) [maximum_resistance=100kΩ]

nets:
  N1: kEYPAD_MATRICIAL_1.col1, Arduino1.D2
  N2: kEYPAD_MATRICIAL_1.arrow1, Arduino1.D3
  N3: kEYPAD_MATRICIAL_1.col2, Arduino1.D4
  N4: kEYPAD_MATRICIAL_1.arrow2, Arduino1.D5
  N5: kEYPAD_MATRICIAL_1.col3, Arduino1.D6
  N6: kEYPAD_MATRICIAL_1.arrow3, Arduino1.D7
  N7: kEYPAD_MATRICIAL_1.arrow4, Arduino1.D8
  N8: J1.pin1, K1.COIL1, S1.L2, Arduino1.GND, LCD1.no_name_yet#100, R8.leg2, R9.leg2
  N9: J1.pin2, R6.leg2
  N10: K1.C1, K1.C2, Arduino1.D11
  N11: K1.COIL2, S1.L1, TRS1.Sleeve, S2.leg1, Arduino1.+5V, LCD1.no_name_yet#101, LCD1.no_name_yet#114, R8.leg1, R9.leg1
  N12: S1.COM, R7.Pin_0
  N13: TRS1.Ring, TRS1.Tip, S2.leg0, R4.Pin_1
  N14: R4.Pin_0, Arduino1.D13
  N15: Arduino1.D12, R6.leg1
  N16: Arduino1.D10, R7.Pin_1
  N17: Arduino1.A0, LCD1.no_name_yet#103
  N18: Arduino1.A1, LCD1.no_name_yet#105
  N19: Arduino1.A2, LCD1.no_name_yet#110
  N20: Arduino1.A3, LCD1.no_name_yet#111
  N21: Arduino1.A4, LCD1.no_name_yet#112
  N22: Arduino1.A5, LCD1.no_name_yet#113
  N23: LCD1.no_name_yet#102, R9.wiper
  N24: LCD1.no_name_yet#115, R8.wiper

notes:
  JACK mono 1/4" female for pedal
  This should be a 4x4 keypad, if only Fritzing had the model
  the ORANGE pot. controls the backlight, the YELLOW one controls the LCD contrast

custom parts:
  KEYPAD 4x3: KEYPAD matricial de 12 botones, 4 filas x 3 columnas
  Adafruit Negative RGB 2x16 LCD: Adafruit Negative 2x16 LCD Display with RGB Backlight
