# Fritzing sketch Schema_DL002A (saved by Fritzing 0.8.3b)
breadboards: 1

parts:
  J1 = Piezo Speaker
  K1 = Relay [part_number=FRS1B-S package=THT]
  S1 = Toggle Switch [package=THT]
  TRS1 = Audio Jack (TRS) 3.5mm [package="4Ucon 08780 [THT]"]
  S2 = Round Pushbutton
  R4 = Resistor [tolerance=±5% resistance=10k package=THT]
  7_Segment1 = 7 Segment Display
  7_Segment2 = 7 Segment Display  # not connected
  7_Segment3 = 7 Segment Display  # not connected
  7_Segment4 = 7 Segment Display
  7_Segment5 = 7 Segment Display
  Arduino1 = Arduino
  R7 = Resistor [tolerance=±5% resistance=330 package=THT]
  R8 = Rotary Potentiometer (Small) [maximum_resistance=100kΩ]
  R6 = Rotary Potentiometer (Small) [maximum_resistance=100kΩ]
  Matrix_keypad1 = KEYPAD 4x4

nets:
  N1: J1.pin1, K1.COIL1, S1.L2, 7_Segment1.Segment_E, 7_Segment4.Segment_C, Arduino1.GND, R8.leg1
  N2: J1.pin2, R6.leg2
  N3: K1.C1, K1.C2, Arduino1.D11
  N4: K1.COIL2, S1.L1, TRS1.Sleeve, S2.leg1, 7_Segment1.Segment_D, 7_Segment4.Segment_DP, Arduino1.+5V, R8.leg2
  N5: TRS1.Ring, TRS1.Tip, S2.leg0, R4.Pin_1
  N6: R4.Pin_0, Arduino1.D13
  N7: 7_Segment4.Segment_B, Arduino1.A1
  N8: 7_Segment4.Segment_A, Arduino1.A0
  N9: 7_Segment5.Segment_C, Arduino1.A2
  N10: Arduino1.D12, R6.leg1
  N11: Arduino1.D10, R7.Pin_1
  N12: Arduino1.D9, Matrix_keypad1.row4
  N13: Arduino1.D8, Matrix_keypad1.row3
  N14: Arduino1.D7, Matrix_keypad1.row2
  N15: Arduino1.D6, Matrix_keypad1.row1
  N16: Arduino1.D5, Matrix_keypad1.col4
  N17: Arduino1.D4, Matrix_keypad1.col3
  N18: Arduino1.D3, Matrix_keypad1.col2
  N19: Arduino1.D2, Matrix_keypad1.col1
  N20: Arduino1.A3, R8.wiper

notes:
  JACK mono 1/4" female for pedal
  Grove LED Bar (serial)
  http://www.seeedstudio.com/wiki/Grove_-_LED_Bar
  wire DI to pin A0
  and DCKI to pin A1
  Sparkfun 7-Segment Serial Display
  https://www.sparkfun.com/products/11441
  Wire RX to pin A2,
  GND and VCC as usual.

custom parts:
  KEYPAD 4x4: Matrix keypad 16 buttons, 4 rows x 4 columns
